# Fritzing sketch light sensor (saved by Fritzing 0.9.4)
breadboards: 1

parts:
  Part1 = Adafruit HUZZAH32 ESP32 Feather [part_number="Adafruit #3405"]
  R1 = Photocell (LDR) [package=THT]
  R2 = Resistor [tolerance=±5% resistance=10k package=THT]

nets:
  N1: Part1.A2_I34, R1.pin_0, R2.Pin_1
  N2: Part1.GND, R1.pin_1
  N3: Part1.3.3V, R2.Pin_0

notes:
  io_pub.py wiring for light sensor using 10K ohm resistor
