# Fritzing sketch pwm (saved by Fritzing 0.9.4)
breadboards: 1

parts:
  Part1 = Adafruit HUZZAH32 ESP32 Feather [part_number="Adafruit #3405"]
  R1 = Rotary Potentiometer (Small) [maximum_resistance=100kΩ package=THT]
  LED1 = LED - 5mm [color="Red (633nm)" package="5 mm [THT]"]

nets:
  N1: Part1.A2_I34, R1.wiper
  N2: Part1.GND, R1.leg2, LED1.cathode
  N3: Part1.3.3V, R1.leg1
  N4: Part1.IO32_A7, LED1.anode

notes:
  pwm.py wiring for potentiometer and LED
