# Fritzing sketch serial-esp32-cpx (saved by Fritzing 0.9.4)
breadboards: 1

parts:
  Part1 = Adafruit HUZZAH32 ESP32 Feather [part_number="Adafruit #3405"]
  Part2 = Adafruit Circuit Playground Express [part_number="Adafruit #3333"]

nets:
  N1: Part1.IO17, Part2.D1_A7_TX
  N2: Part1.IO16, Part2.D0_A6_RX
  GND: Part1.GND, Part2.GND

notes:
  serial connect between ESP32 and CPX - TX->RX, RX->TX

custom parts:
  Adafruit Circuit Playground Express: Circuit Playground Express is the next step towards a perfect introduction to electronics and programming. We've taken the original Circuit Playground Classic and made it even better! Not only did we pack even more sensors in, we also made it even easier to program. You can now start your journey with Microsoft MakeCode block-based or Javascript programming. Then, you can use the same board to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
