# Fritzing sketch servo-externalpwr (saved by Fritzing 0.9.4)
breadboards: 1

parts:
  Part1 = Adafruit HUZZAH32 ESP32 Feather [part_number="Adafruit #3405"]
  VCC1 = 4 x AAA Battery Mount
  J1 = Basic Servo
  J3 = Basic Servo

nets:
  GND: Part1.GND, VCC1.-, J1.gnd, J3.gnd
  N1: Part1.IO15_A8, J1.pulse
  N2: Part1.IO32_A7, J3.pulse
  N3: VCC1.+, J3.vcc

notes:
  servo_move.py wiring with two servos and external power from battery
